// Logisim project s-mips.circ as structural Verilog: 15 circuits, main circuit S-MIPS Board
module S_MIPS_Board (
  input  DESHABILITAR_DISPATCHER,
  output halt
);

  wire button_1_out, CLK, CS, d_ff_1_q, LCLR, LoadRAM, LoadRAMOn, LW, R_R_W, R_W, ram_dispatcher_1_finished,
       RCS, Reset_out, RST, TTY_EN;
  wire [2:0] KDB;
  wire [3:0] LMask, Mask, ram_1_read_time, ram_1_write_time, RMask;
  wire [6:0] KDB_DATA, TTY_DATA;
  wire [15:0] Addr, LAddr, RAddr;
  wire [31:0] I0, I1, I2, I3, LData, ram_1_data_out_0, ram_1_data_out_1, ram_1_data_out_2, ram_1_data_out_3,
       RI0, RI1, RI2, RI3;

  TTY #(.rows(25), .cols(80)) tty_1 (.data(TTY_DATA), .clk(CLK), .we(TTY_EN), .clr(RST));
  not not_1 (LoadRAMOn, ram_dispatcher_1_finished);
  RAM_Dispatcher ram_dispatcher_1 (
    .WriteTime(ram_1_write_time), .Clock(CLK), .Data(LData), .Address(LAddr), .Mask(LMask),
    .Finished(ram_dispatcher_1_finished), .Write(LW), .CLR(LCLR));
  Keyboard #(.buflen(64)) keyboard_1 (.clk(CLK), .re(KDB[0]), .clr(KDB[1]), .avail(KDB[2]), .data(KDB_DATA));
  RAM ram_1 (
    .Address(RAddr), .Data_Out_0(ram_1_data_out_0), .Data_Out_1(ram_1_data_out_1),
    .Data_Out_2(ram_1_data_out_2), .Data_Out_3(ram_1_data_out_3), .Data_In_0(RI0), .Data_In_1(RI1),
    .Data_In_2(RI2), .Data_In_3(RI3), .Mask(RMask), .nRead_Write(R_R_W), .Chip_Select(RCS),
    .Read_Time(ram_1_read_time), .Reset(button_1_out), .Write_Time(ram_1_write_time));
  Button button_1 (.out(button_1_out));
  D_Flip_Flop d_ff_1 (.clk(CLK), .D(1'b1), .Q(d_ff_1_q), .reset(Reset_out));  // open: Qn, preset, en
  Button Reset (.out(Reset_out));
  S_MIPS s_mips_1 (
    .Kbd_Enable(KDB[0]), .Address(Addr), .Kbd_Clear(KDB[1]), .Kbd_Available(KDB[2]), .RAM_In_0(I0),
    .Kbd_ASCII_Data(KDB_DATA), .RAM_In_1(I1), .TTY_Enable(TTY_EN), .RAM_In_2(I2), .RAM_In_3(I3),
    .TTY_ASCII_Data(TTY_DATA), .Reset(RST), .RAM_Out_0(ram_1_data_out_0), .Clock(CLK),
    .RAM_Out_1(ram_1_data_out_1), .Stop(halt), .RAM_Out_2(ram_1_data_out_2), .RAM_Out_3(ram_1_data_out_3),
    .Mask(Mask), .Read_Time(ram_1_read_time), .Write_Time(ram_1_write_time), .nRead_Write(R_W),
    .Chip_Select(CS));
  D_Flip_Flop d_ff_2 (.clk(CLK), .D(d_ff_1_q), .Qn(LCLR), .reset(Reset_out));  // open: Q, preset, en
  or or_1 (RST, LCLR, LoadRAM);
  Clock clock_1 (.out(CLK));
  Multiplexer #(.width(32), .enable("false")) multiplexer_1 (.in0(I0), .in1(LData), .out(RI0), .sel(LoadRAM));
  Multiplexer #(.width(32), .enable("false")) multiplexer_2 (.in0(I1), .in1(LData), .out(RI1), .sel(LoadRAM));
  Multiplexer #(.width(32), .enable("false")) multiplexer_3 (.in0(I2), .in1(LData), .out(RI2), .sel(LoadRAM));
  Multiplexer #(.width(32), .enable("false")) multiplexer_4 (.in0(I3), .in1(LData), .out(RI3), .sel(LoadRAM));
  and and_1 (LoadRAM, ~DESHABILITAR_DISPATCHER, LoadRAMOn);  // AND_Gate
  Multiplexer #(.width(16), .enable("false")) multiplexer_5 (.in0(Addr), .in1(LAddr), .out(RAddr), .sel(LoadRAM));
  Multiplexer #(.width(4), .enable("false")) multiplexer_6 (.in0(Mask), .in1(LMask), .out(RMask), .sel(LoadRAM));
  Multiplexer #(.enable("false")) multiplexer_7 (.in0(CS), .in1(LW), .out(RCS), .sel(LoadRAM));
  Multiplexer #(.enable("false")) multiplexer_8 (.in0(R_W), .in1(LW), .out(R_R_W), .sel(LoadRAM));

  // Notes on the sheet:
  //   NO MODIFICAR
  //   Keyboard
endmodule

module RAM (
  input  [15:0] Address,
  input  [31:0] Data_In_0,
  input  [31:0] Data_In_1,
  input  [31:0] Data_In_2,
  input  [31:0] Data_In_3,
  input  [3:0] Mask,
  input  nRead_Write,
  input  Chip_Select,
  input  Reset,
  output [31:0] Data_Out_0,
  output [31:0] Data_Out_1,
  output [31:0] Data_Out_2,
  output [31:0] Data_Out_3,
  output [3:0] Read_Time,
  output [3:0] Write_Time
);

  wire and_2_out, and_3_out, and_4_out, and_5_out, and_6_out, and_7_out, and_8_out, and_9_out, Changed, CLK,
       comparator_2_eq, comparator_3_eq, comparator_4_eq, comparator_5_eq, comparator_6_eq, Count,
       demultiplexer_3_out0, Idle, Idle_q, Load, Load0, Load1, nand_1_out, or_1_out, or_2_out, or_3_out,
       or_4_out, or_5_out, or_6_out, or_7_out, or_8_out, or_9_out, or_10_out, Proc_q, Update_Mem, Zero_Time;
  wire [3:0] counter_1_q, multiplexer_1_out, subtractor_1_out;
  wire [31:0] register_1_q, register_2_q, register_3_q, register_4_q, register_5_q;

  // Probe on 4'b0011
  // Probe on 4'b0010
  Multiplexer #(.width(4), .enable("false")) multiplexer_1 (
    .in0(4'b0011), .in1(4'b0010), .out(multiplexer_1_out), .sel(nRead_Write));
  or or_1 (or_1_out, Idle, Update_Mem);
  or or_2 (or_2_out, ~Chip_Select, Reset);  // OR_Gate
  Subtractor #(.width(4)) subtractor_1 (.a(multiplexer_1_out), .b(4'b0010), .out(subtractor_1_out));  // open: bin, bout
  D_Flip_Flop u_Idle (.clk(CLK), .D(or_1_out), .Q(Idle_q), .preset(or_2_out));  // open: Qn, en, reset
  Demultiplexer #(.enable("false")) demultiplexer_1 (.out0(Idle), .out1(Load0), .in(Idle_q), .sel(Changed));
  // Probe on counter_1_q
  Counter #(.width(4), .max('hf)) counter_1 (
    .load(Load), .D(subtractor_1_out), .count(Count), .Q(counter_1_q), .clk(CLK), .clr(or_3_out));  // open: carry
  or or_3 (or_3_out, ~Chip_Select, Reset);  // OR_Gate
  Comparator #(.width(4), .mode("unsigned")) comparator_1 (
    .a(4'b0000), .b(counter_1_q), .eq(Zero_Time));  // open: gt, lt
  or or_4 (or_4_out, Count, Load0, Load1);
  Register #(.width(32)) register_1 (.D(Data_In_0), .en(Chip_Select), .Q(register_1_q), .clk(CLK), .clr(or_5_out));
  or or_5 (or_5_out, ~Chip_Select, Reset);  // OR_Gate
  Register #(.width(32)) register_2 (.D(Data_In_1), .en(Chip_Select), .Q(register_2_q), .clk(CLK), .clr(or_6_out));
  or or_6 (or_6_out, ~Chip_Select, Reset);  // OR_Gate
  Register #(.width(32)) register_3 (.D(Data_In_2), .en(Chip_Select), .Q(register_3_q), .clk(CLK), .clr(or_7_out));
  or or_7 (or_7_out, ~Chip_Select, Reset);  // OR_Gate
  Register #(.width(32)) register_4 (.D(Data_In_3), .en(Chip_Select), .Q(register_4_q), .clk(CLK), .clr(or_8_out));
  or or_8 (or_8_out, ~Chip_Select, Reset);  // OR_Gate
  Register #(.width(32)) register_5 (
    .D({{11{1'b1}}, nRead_Write, Mask, Address}), .en(Chip_Select), .Q(register_5_q), .clk(CLK),
    .clr(or_9_out));
  or or_9 (or_9_out, ~Chip_Select, Reset);  // OR_Gate
  D_Flip_Flop Proc (.clk(CLK), .D(or_4_out), .Q(Proc_q), .reset(or_10_out));  // open: Qn, preset, en
  or or_10 (or_10_out, ~Chip_Select, Reset);  // OR_Gate
  Demultiplexer #(.enable("false")) demultiplexer_2 (
    .out0(Count), .out1(Update_Mem), .in(demultiplexer_3_out0), .sel(Zero_Time));
  Demultiplexer #(.enable("false")) demultiplexer_3 (
    .out0(demultiplexer_3_out0), .out1(Load1), .in(Proc_q), .sel(Changed));
  Clock clock_1 (.out(CLK));
  Comparator #(.width(32)) comparator_2 (.a(register_1_q), .b(Data_In_0), .eq(comparator_2_eq));  // open: gt, lt
  Comparator #(.width(32)) comparator_3 (.a(register_2_q), .b(Data_In_1), .eq(comparator_3_eq));  // open: gt, lt
  Comparator #(.width(32)) comparator_4 (.a(register_3_q), .b(Data_In_2), .eq(comparator_4_eq));  // open: gt, lt
  Comparator #(.width(32)) comparator_5 (.a(register_4_q), .b(Data_In_3), .eq(comparator_5_eq));  // open: gt, lt
  Comparator #(.width(32)) comparator_6 (
    .a(register_5_q), .b({{11{1'b1}}, nRead_Write, Mask, Address}), .eq(comparator_6_eq));  // open: gt, lt
  nand nand_1 (nand_1_out, comparator_6_eq, comparator_2_eq, comparator_3_eq, comparator_4_eq, comparator_5_eq);
  and and_1 (Changed, nand_1_out, Chip_Select);
  or or_11 (Load, Count, Load1, Load0);
  and and_2 (and_2_out, Mask[0], Update_Mem, nRead_Write);
  and and_3 (and_3_out, Mask[1], Update_Mem, nRead_Write);
  and and_4 (and_4_out, Mask[2], Update_Mem, nRead_Write);
  and and_5 (and_5_out, Mask[3], Update_Mem, nRead_Write);
  RAM_part #(.addrWidth(16), .dataWidth(32), .bus("separate")) ram_1 (
    .addr(Address), .din(Data_In_0), .data(Data_Out_0), .str(and_2_out), .sel(Chip_Select), .clk(CLK),
    .ld(and_6_out), .clr(Reset));
  and and_6 (and_6_out, ~nRead_Write, Idle);  // AND_Gate
  RAM_part #(.addrWidth(16), .dataWidth(32), .bus("separate")) ram_2 (
    .addr(Address), .din(Data_In_1), .data(Data_Out_1), .str(and_3_out), .sel(Chip_Select), .clk(CLK),
    .ld(and_7_out), .clr(Reset));
  and and_7 (and_7_out, ~nRead_Write, Idle);  // AND_Gate
  RAM_part #(.addrWidth(16), .dataWidth(32), .bus("separate")) ram_3 (
    .addr(Address), .din(Data_In_2), .data(Data_Out_2), .str(and_4_out), .sel(Chip_Select), .clk(CLK),
    .ld(and_8_out), .clr(Reset));
  and and_8 (and_8_out, ~nRead_Write, Idle);  // AND_Gate
  RAM_part #(.addrWidth(16), .dataWidth(32), .bus("separate")) ram_4 (
    .addr(Address), .din(Data_In_3), .data(Data_Out_3), .str(and_5_out), .sel(Chip_Select), .clk(CLK),
    .ld(and_9_out), .clr(Reset));
  and and_9 (and_9_out, ~nRead_Write, Idle);  // AND_Gate

  assign Read_Time = 4'b0011;
  assign Write_Time = 4'b0010;

  // Other names for the same wires on the sheet: M0 = Mask[0]; M1 = Mask[1]; M2 = Mask[2]; M3 = Mask[3];
  //   RW = nRead_Write; CLR = Reset; CS = Chip_Select; Load2 = Count

  // Notes on the sheet:
  //   NO MODIFICAR
  //   excepto quizás los valores RT y WT
  //   BANK0
  //   BANK1
  //   BANK2
  //   BANK3
endmodule

module RAM_Dispatcher (
  input  [3:0] WriteTime,
  input  Clock,
  input  CLR,
  output [31:0] Data,
  output [15:0] Address,
  output [3:0] Mask,
  output Finished,
  output Write
);

  wire demultiplexer_2_out1, demultiplexer_3_out1, End, IDLE_q, IncAddr, Load, or_1_out, or_2_out, While_q,
       WriteEnd;
  wire [3:0] counter_1_q;
  wire [31:0] CurrentAddress_q;

  Counter #(.width(32), .max('hffffffff)) CurrentAddress (
    .count(IncAddr), .Q({CurrentAddress_q[31:18], Address, CurrentAddress_q[1:0]}), .clk(Clock), .clr(CLR));  // open: load, D, carry
  or or_1 (or_1_out, IncAddr, demultiplexer_3_out1, Finished);
  D_Flip_Flop IDLE (.clk(Clock), .D(or_1_out), .Q(IDLE_q), .preset(CLR));  // open: Qn, en, reset
  Demultiplexer #(.enable("false")) demultiplexer_1 (.out0(Load), .out1(Finished), .in(IDLE_q), .sel(End));
  D_Flip_Flop While (.clk(Clock), .D(or_2_out), .Q(While_q), .reset(CLR));  // open: Qn, preset, en
  or or_2 (or_2_out, Write, Load);
  RAM_part #(.addrWidth(18), .dataWidth(32)) ram_1 (
    .addr({Address, CurrentAddress_q[1:0]}), .data(Data), .clk(Clock));  // open: sel, ld, clr
  Demultiplexer #(.enable("false")) demultiplexer_2 (
    .out0(Write), .out1(demultiplexer_2_out1), .in(While_q), .sel(WriteEnd));
  Decoder #(.select(2)) decoder_1 (
    .out0(Mask[0]), .out1(Mask[1]), .out2(Mask[2]), .out3(Mask[3]), .sel(CurrentAddress_q[1:0]));  // open: en
  Demultiplexer #(.enable("false")) demultiplexer_3 (
    .out0(IncAddr), .out1(demultiplexer_3_out1), .in(demultiplexer_2_out1), .sel(End));
  Counter #(.width(4), .max('hf)) counter_1 (
    .load(Load), .D(WriteTime), .count(Write), .Q(counter_1_q), .clk(Clock));  // open: carry, clr
  Comparator #(.width(32)) comparator_1 (.a(Data), .b({32{1'b1}}), .eq(End));  // open: gt, lt
  Comparator #(.width(4)) comparator_2 (.a(4'b0000), .b(counter_1_q), .eq(WriteEnd));  // open: gt, lt

  // Other names for the same wires on the sheet: CLK = Clock; Count = Write; WT[3:0] = WriteTime
endmodule

module Borrador (
);

  wire [31:0] shifter_1_out;

  Shifter #(.width(32)) shifter_1 (.in({32{1'b1}}), .\dist (5'b00010), .out(shifter_1_out));
  // Probe on shifter_1_out
endmodule

module S_MIPS (
  input  Kbd_Available,
  input  [6:0] Kbd_ASCII_Data,
  input  [31:0] RAM_Out_0,
  input  [31:0] RAM_Out_1,
  input  Reset,
  input  [31:0] RAM_Out_2,
  input  Clock,
  input  [31:0] RAM_Out_3,
  input  [3:0] Read_Time,
  input  [3:0] Write_Time,
  output Kbd_Enable,
  output [15:0] Address,
  output Kbd_Clear,
  output TTY_Enable,
  output [6:0] TTY_ASCII_Data,
  output Stop,
  output [31:0] RAM_In_0,
  output [31:0] RAM_In_1,
  output [31:0] RAM_In_2,
  output [31:0] RAM_In_3,
  output [3:0] Mask,
  output nRead_Write,
  output Chip_Select
);

  wire and_1_out, and_2_out, and_3_out, cronometro_1_contando, cronometro_2_contando, cronometro_3_contando,
       instruction_decoder_1_escribir_en_ram, instruction_decoder_1_inm, instruction_decoder_1_leer_ram,
       instruction_decoder_1_save, instruction_decoder_1_variara_sp, JC, JI, JO, or_1_out, Rd,
       reader_1_out_15, RF, WF, Wr;
  wire [1:0] priority_encoder_1_out;
  wire [4:0] instruction_decoder_1_a, instruction_decoder_1_b, instruction_decoder_1_da, Op, reader_1_out_14;
  wire [31:0] A, B, branch_control_1_output, C, Instr, JS, k, LDLR, RAddress, reader_1_out_12, WAddress;

  instruction_decoder instruction_decoder_1 (
    .in_1(Instr), .jump(JI), .out_4(Op), .DA(instruction_decoder_1_da), .Inm(instruction_decoder_1_inm),
    .j_override(JO), .VARIARA_SP(instruction_decoder_1_variara_sp), .B(instruction_decoder_1_b),
    .A(instruction_decoder_1_a), .k(k), .save(instruction_decoder_1_save),
    .LEER_RAM(instruction_decoder_1_leer_ram), .ESCRIBIR_EN_RAM(instruction_decoder_1_escribir_en_ram));
  and and_1 (and_1_out, ~WF, ~RF, JC);  // AND_Gate
  READER reader_1 (
    .in_10(instruction_decoder_1_da), .ALU(C), .in_8(LDLR), .DEBE_GUARDARSE(instruction_decoder_1_save),
    .in_6(RF), .in_7(Clock), .in_9(Reset), .out_14(reader_1_out_14), .out_12(reader_1_out_12),
    .out_15(reader_1_out_15), .in_1(A), .in_2(B), .in_3(k), .in_5(Op), .out_13(RAddress));
  Cronometro cronometro_1 (
    .in_1(Write_Time), .EMPEZAR(instruction_decoder_1_escribir_en_ram), .FIN(WF), .RELOJ(Clock),
    .RESET(Reset), .CONTANDO(cronometro_1_contando));
  Priority_Encoder #(.select(2)) priority_encoder_1 (
    .in0(Mask[0]), .in1(Mask[1]), .in2(Mask[2]), .in3(Mask[3]), .out(priority_encoder_1_out));  // open: gs, en_out, en_in
  Cronometro cronometro_2 (
    .in_1(Read_Time), .EMPEZAR(instruction_decoder_1_leer_ram), .FIN(RF), .RELOJ(Clock), .RESET(Reset),
    .CONTANDO(cronometro_2_contando));
  D_Flip_Flop #(.trigger("falling")) d_ff_1 (
    .clk(Clock), .D(and_2_out), .Q(Wr), .en(cronometro_1_contando), .reset(Reset));  // open: Qn, preset
  and and_2 (and_2_out, cronometro_1_contando, ~WF);  // AND_Gate
  Branch_control branch_control_1 (
    .INSTRUC(JI), .COND(and_1_out), .CLK(Clock), .RST(Reset), .Output(branch_control_1_output), .inst_J(JO),
    .in_1(JS));
  D_Flip_Flop #(.trigger("falling")) d_ff_2 (
    .clk(Clock), .D(and_3_out), .Q(Rd), .en(cronometro_2_contando), .reset(Reset));  // open: Qn, preset
  and and_3 (and_3_out, cronometro_2_contando, ~RF);  // AND_Gate
  Register_File register_file_1 (
    .in_6(reader_1_out_14), .in_7(reader_1_out_15), .in_4(reader_1_out_12), .INPUTS(instruction_decoder_1_a),
    .in_5(Clock), .in_2(instruction_decoder_1_b), .A(A), .B(B), .in_3(Reset),
    .in_8(instruction_decoder_1_variara_sp));
  or or_1 (or_1_out, Reset, Stop);
  Program_counter program_counter_1 (
    .in_3(RAM_Out_0), .ENTRADAS(Read_Time), .in_5(Rd), .in_8(RAM_Out_1), .in_7(Wr), .in_9(RAM_Out_2),
    .in_11(RAM_Out_3), .out_12(LDLR), .out_13(Instr), .in_2(Clock), .in_4(or_1_out),
    .RAM(priority_encoder_1_out), .in_10(cronometro_3_contando));
  WRITER writer_1 (
    .in_2(k), .in_1(A), .in_3(Clock), .in_4(Reset), .in_5(B), .in_6(Op), .out_8(RAM_In_0), .SALIDA(RAM_In_1),
    .out_7(WAddress), .out_10(RAM_In_2), .out_11(RAM_In_3));
  GET_RAM_ADDRESS get_ram_address_1 (
    .in_6(Rd), .in_1(branch_control_1_output), .in_2(RAddress), .in_3(WAddress), .RAM_Address(Address),
    .in_5(Wr), .RAM_MASK(Mask), .rst(cronometro_3_contando));
  ALU alu_1 (
    .in_1(A), .in_2(B), .Result(C), .in_8(Op), .in_5(Clock), .Cond(JC), .Jump_size(JS), .Stop(Stop),
    .Enable(TTY_Enable), .TTY(TTY_ASCII_Data), .in_7(Kbd_Available), .in_6(Kbd_ASCII_Data), .in_9(Reset),
    .in_3(k), .in_4(instruction_decoder_1_inm));
  Multiplexer #(.enable("false")) multiplexer_1 (.in0(Wr), .in1(1'b0), .out(nRead_Write), .sel(cronometro_3_contando));
  Cronometro cronometro_3 (
    .in_1(Read_Time), .EMPEZAR(Reset), .RELOJ(Clock), .RESET(1'b0), .CONTANDO(cronometro_3_contando));  // open: FIN

  assign Chip_Select = 1'b1;

  // Other names for the same wires on the sheet: CLK = Clock; CLR = Reset; KBD_AVAIL = Kbd_Available;
  //   KBD_CLR = Kbd_Clear; KBD_DATA[6:0] = Kbd_ASCII_Data; RAM_A[15:0] = Address; RAM_INPUT_0[31:0] = RAM_In_0;
  //   RAM_INPUT_1[31:0] = RAM_In_1; RAM_INPUT_2[31:0] = RAM_In_2; RAM_INPUT_3[31:0] = RAM_In_3; RAM_MASK[3:0] = Mask;
  //   RAM_OUTPUT_0[31:0] = RAM_Out_0; RAM_OUTPUT_1[31:0] = RAM_Out_1; RAM_OUTPUT_2[31:0] = RAM_Out_2;
  //   RAM_OUTPUT_3[31:0] = RAM_Out_3; RW = nRead_Write; TTY_DATA[6:0] = TTY_ASCII_Data

  // Notes on the sheet:
  //   RAM ADDRESS
  //   DATA FROM RAM
  //   DATA TO RAM
  //   DATA WRITE MASK
  //   RAM TIMING
  //   RAM CONTROL
  //   KEYBOARD
  //   TTY
  //   SEQUENCING
endmodule

module Cronometro (
  input  [3:0] in_1,
  input  EMPEZAR,
  input  RELOJ,
  input  RESET,
  output FIN,
  output CONTANDO
);

  wire comparator_1_eq, comparator_2_lt, d_ff_1_q, or_1_out;
  wire [4:0] counter_1_q;

  D_Flip_Flop #(.trigger("falling")) d_ff_1 (
    .clk(RELOJ), .D(EMPEZAR), .Q(d_ff_1_q), .preset(1'b0), .en(EMPEZAR), .reset(or_1_out));  // open: Qn
  Counter #(.width(5), .max('h1f)) counter_1 (
    .load(1'b0), .count(d_ff_1_q), .Q(counter_1_q), .clk(RELOJ), .clr(or_1_out));  // open: D, carry
  or or_1 (or_1_out, comparator_2_lt, RESET);
  Comparator #(.width(5)) comparator_1 (.a(counter_1_q), .b({5{1'b0}}), .eq(comparator_1_eq));  // open: gt, lt
  Comparator #(.width(5)) comparator_2 (.a({1'b0, in_1}), .b(counter_1_q), .eq(FIN), .lt(comparator_2_lt));  // open: gt
  or or_2 (CONTANDO, ~comparator_1_eq, EMPEZAR);  // OR_Gate

  // Notes on the sheet:
  //   Cronometro
endmodule

module Branch_control (
  input  [31:0] in_1,
  input  CLK,
  input  RST,
  input  inst_J,
  input  INSTRUC,
  input  COND,
  output [31:0] Output
);

  wire and_1_out;
  wire [5:0] shifter_2_out_2;
  wire [25:0] shifter_2_out;
  wire [31:0] adder_1_out, adder_2_out, multiplexer_1_out, multiplexer_2_out, shifter_1_out;

  Shifter #(.width(32)) shifter_1 (.in(in_1), .\dist (5'b00010), .out(shifter_1_out));
  Adder #(.width(32)) adder_1 (.a(Output), .b(32'h4), .out(adder_1_out));  // open: cin, cout
  Multiplexer #(.width(32), .enable("false")) multiplexer_1 (
    .in0({32{1'b0}}), .in1(shifter_1_out), .out(multiplexer_1_out), .sel(and_1_out));
  and and_1 (and_1_out, INSTRUC, COND);
  Adder #(.width(32)) adder_2 (.a(adder_1_out), .b(multiplexer_1_out), .out(adder_2_out));  // open: cin, cout
  Shifter #(.width(32)) shifter_2 (.in(in_1), .\dist (5'b00010), .out({shifter_2_out_2, shifter_2_out}));
  // Probe on Output
  Register #(.width(32)) register_1 (.D(multiplexer_2_out), .en(1'b1), .Q(Output), .clk(CLK), .clr(RST));
  Multiplexer #(.select(2), .width(32), .enable("false")) multiplexer_2 (
    .in0(adder_2_out), .in1(adder_2_out), .in2({Output[31:26], shifter_2_out}), .in3(in_1),
    .out(multiplexer_2_out), .sel({inst_J, COND}));

  // Other names for the same wires on the sheet: next[31:0] = Output; IN[31:0] = in_1

  // Notes on the sheet:
  //   SALTO
  //   SUMA 4
  //   SUMA SALTO
  //   SALTO
  //   BRANCH CONTROL
  //   CONTADOR
  //   PROXIMA
  //   PROXIMA
  //   INSTRUCCION
endmodule

// Saca 1 cuando termino de cargar la instruccion
module Program_counter (
  input  [3:0] ENTRADAS,
  input  in_2,
  input  [31:0] in_3,
  input  in_4,
  input  in_5,
  input  [1:0] RAM,
  input  in_7,
  input  [31:0] in_8,
  input  [31:0] in_9,
  input  in_10,
  input  [31:0] in_11,
  output [31:0] out_12,
  output [31:0] out_13
);

  wire and_1_out, cronometro_1_contando, cronometro_1_fin, Enable, nor_1_out, not_1_out;

  Multiplexer #(.select(2), .width(32), .enable("false")) multiplexer_1 (
    .in0(in_3), .in1(in_8), .in2(in_9), .in3(in_11), .out(out_12), .sel(RAM));
  Multiplexer #(.width(32), .enable("false")) multiplexer_2 (
    .in0(32'hffff0010), .in1(out_12), .out(out_13), .sel(nor_1_out));
  nor nor_1 (nor_1_out, in_10, Enable, and_1_out);
  and and_1 (and_1_out, cronometro_1_contando, ~cronometro_1_fin);  // AND_Gate
  not not_1 (not_1_out, in_10);
  Cronometro cronometro_1 (
    .in_1(ENTRADAS), .EMPEZAR(not_1_out), .FIN(cronometro_1_fin), .RELOJ(in_2), .RESET(Enable),
    .CONTANDO(cronometro_1_contando));
  or or_1 (Enable, in_4, in_5, in_7);

  // Other names for the same wires on the sheet: CLK = in_2; RST = in_4; RT[3:0] = ENTRADAS

  // Notes on the sheet:
  //   B0
  //   B1
  //   B2
  //   B3
  //   MASK
  //   PROGRAM COUNTER
  //   READED FROM RAM
  //   NEXT INSTRUCTION
endmodule

module GET_RAM_ADDRESS (
  input  [31:0] in_1,
  input  [31:0] in_2,
  input  [31:0] in_3,
  input  rst,
  input  in_5,
  input  in_6,
  output [3:0] RAM_MASK,
  output [15:0] RAM_Address
);

  wire [1:0] multiplexer_2_out;
  wire [31:0] multiplexer_1_out;

  Multiplexer #(.select(2), .width(32), .enable("false")) multiplexer_1 (
    .in0(in_1), .in1(in_2), .in2(in_3),
    .out({multiplexer_1_out[31:20], RAM_Address, multiplexer_1_out[3:0]}), .sel(multiplexer_2_out));  // open: in3
  Multiplexer #(.width(2), .enable("false")) multiplexer_2 (
    .in0({in_5, in_6}), .in1(2'b00), .out(multiplexer_2_out), .sel(rst));
  Demultiplexer #(.select(2), .enable("false")) demultiplexer_1 (
    .out0(RAM_MASK[0]), .out1(RAM_MASK[1]), .out2(RAM_MASK[2]), .out3(RAM_MASK[3]), .in(1'b1),
    .sel(multiplexer_1_out[3:2]));

  // Notes on the sheet:
  //   CB INSTRUCTION
  //   READ INSTRUCTION
  //   WRITE INSTRUCTION
  //   RAM ADDRESS
endmodule

module instruction_decoder (
  input  [31:0] in_1,
  output j_override,
  output jump,
  output [4:0] out_4,
  output [4:0] DA,
  output save,
  output [31:0] k,
  output [4:0] A,
  output Inm,
  output [4:0] B,
  output ESCRIBIR_EN_RAM,
  output VARIARA_SP,
  output LEER_RAM
);

  wire add, \and , and_2_out, and_3_out, and_11_out, and_12_out, and_13_out, and_14_out, and_15_out,
       and_17_out, and_18_out, and_19_out, and_21_out, beq, bgtz, blez, bltz, bne, comparator_1_gt,
       comparator_2_eq, comparator_3_gt, comparator_4_eq, comparator_5_eq, comparator_6_eq, comparator_7_eq,
       comparator_9_eq, comparator_10_eq, comparator_14_eq, comparator_15_eq, comparator_16_eq,
       comparator_17_eq, comparator_18_eq, comparator_19_eq, comparator_20_eq, comparator_23_eq,
       comparator_24_eq, comparator_25_eq, comparator_26_eq, comparator_27_eq, comparator_29_eq,
       comparator_30_eq, comparator_31_gt, comparator_32_gt, comparator_32_lt, comparator_33_gt,
       comparator_35_eq, comparator_36_eq, comparator_38_eq, comparator_39_eq, comparator_40_eq,
       comparator_41_eq, comparator_42_eq, comparator_44_eq, comparator_45_eq, comparator_46_eq,
       comparator_47_eq, comparator_48_eq, comparator_49_eq, div, divu, halt, j, jr, kbd, lw, mfhi, mflo,
       mul, mulu, \nor , nor_1_out, nor_2_out, OPCODE_0, \or , or_1_out, or_3_out, or_5_out, or_6_out,
       or_7_out, pop, push, rnd, stl, stlu, sub, sw, tty, \xor ;
  wire [15:0] multiplexer_3_out;

  Multiplexer #(.width(5), .enable("false")) multiplexer_1 (.in0(in_1[12:8]), .in1({5{1'b1}}), .out(B), .sel(or_1_out));
  or or_1 (or_1_out, push, pop);
  // Probe on in_1
  Comparator #(.width(6)) comparator_1 (.a(6'b001111), .b(in_1[7:2]), .gt(comparator_1_gt));  // open: eq, lt
  Comparator #(.width(6)) comparator_2 (.a(in_1[7:2]), .b(6'b001001), .eq(comparator_2_eq));  // open: gt, lt
  Comparator #(.width(6)) comparator_3 (.a(in_1[7:2]), .b(6'b000111), .gt(comparator_3_gt));  // open: eq, lt
  Comparator #(.width(11)) comparator_4 (
    .a(11'h20), .b({in_1[18:16], in_1[31:24]}), .eq(comparator_4_eq));  // open: gt, lt
  Comparator #(.width(6)) comparator_5 (.a(6'b001000), .b(in_1[7:2]), .eq(comparator_5_eq));  // open: gt, lt
  Comparator #(.width(16)) comparator_6 (
    .a(16'h18), .b({in_1[23:16], in_1[31:24]}), .eq(comparator_6_eq));  // open: gt, lt
  Comparator #(.width(16)) comparator_7 (
    .a(16'h19), .b({in_1[23:16], in_1[31:24]}), .eq(comparator_7_eq));  // open: gt, lt
  Comparator #(.width(32)) comparator_8 (.a(in_1), .b(32'h3f0000fc), .eq(halt));  // open: gt, lt
  Comparator #(.width(16)) comparator_9 (
    .a(16'hfc00), .b({in_1[7:0], in_1[15:8]}), .eq(comparator_9_eq));  // open: gt, lt
  and and_1 (rnd, comparator_9_eq, comparator_10_eq);
  Comparator #(.width(11)) comparator_10 (
    .a(11'h2), .b({in_1[18:16], in_1[31:24]}), .eq(comparator_10_eq));  // open: gt, lt
  and and_2 (and_2_out, comparator_1_gt, ~comparator_2_eq, comparator_3_gt);  // AND_Gate
  and and_3 (and_3_out, OPCODE_0, comparator_4_eq);
  or or_2 (add, and_3_out, comparator_5_eq);
  and and_4 (mul, OPCODE_0, comparator_6_eq);
  and and_5 (mulu, OPCODE_0, comparator_7_eq);
  Comparator #(.width(6)) comparator_11 (.a(6'b000100), .b(in_1[7:2]), .eq(beq));  // open: gt, lt
  Comparator #(.width(6)) comparator_12 (.a(6'b000101), .b(in_1[7:2]), .eq(bne));  // open: gt, lt
  Multiplexer #(.width(5), .enable("false")) multiplexer_2 (
    .in0(in_1[23:19]), .in1(in_1[12:8]), .out(DA), .sel(or_3_out));
  or or_3 (or_3_out, and_2_out, lw);
  Comparator #(.width(6)) comparator_13 (.a(in_1[7:2]), .b({6{1'b0}}), .eq(OPCODE_0));  // open: gt, lt
  Comparator #(.width(16)) comparator_14 (
    .a(16'hfc00), .b({in_1[7:0], in_1[15:8]}), .eq(comparator_14_eq));  // open: gt, lt
  Comparator #(.width(11)) comparator_15 (
    .a(11'h4), .b({in_1[18:16], in_1[31:24]}), .eq(comparator_15_eq));  // open: gt, lt
  and and_6 (sub, OPCODE_0, comparator_16_eq);
  Comparator #(.width(11)) comparator_16 (
    .a(11'h22), .b({in_1[18:16], in_1[31:24]}), .eq(comparator_16_eq));  // open: gt, lt
  and and_7 (div, OPCODE_0, comparator_17_eq);
  Comparator #(.width(16)) comparator_17 (
    .a(16'h1a), .b({in_1[23:16], in_1[31:24]}), .eq(comparator_17_eq));  // open: gt, lt
  and and_8 (divu, OPCODE_0, comparator_18_eq);
  Comparator #(.width(16)) comparator_18 (
    .a(16'h1b), .b({in_1[23:16], in_1[31:24]}), .eq(comparator_18_eq));  // open: gt, lt
  and and_9 (kbd, comparator_14_eq, comparator_15_eq);
  Comparator #(.width(6)) comparator_19 (.a({6{1'b1}}), .b(in_1[7:2]), .eq(comparator_19_eq));  // open: gt, lt
  and and_10 (tty, comparator_19_eq, comparator_20_eq);
  Comparator #(.width(21)) comparator_20 (
    .a(21'h1), .b({in_1[12:8], in_1[23:16], in_1[31:24]}), .eq(comparator_20_eq));  // open: gt, lt
  Comparator #(.width(6)) comparator_21 (.a(6'b000110), .b(in_1[7:2]), .eq(blez));  // open: gt, lt
  Comparator #(.width(6)) comparator_22 (.a(6'b000111), .b(in_1[7:2]), .eq(bgtz));  // open: gt, lt
  or or_4 (j_override, j, jr);
  and and_11 (and_11_out, in_1[2], in_1[3], in_1[4]);
  and and_12 (and_12_out, in_1[5], in_1[6], in_1[7]);
  Multiplexer #(.width(16), .enable("false")) multiplexer_3 (
    .in0({16{1'b0}}), .in1({16{1'b1}}), .out(multiplexer_3_out), .sel(in_1[23]));
  Comparator #(.width(6)) comparator_23 (.a(6'b000111), .b(in_1[7:2]), .eq(comparator_23_eq));  // open: gt, lt
  or or_5 (or_5_out, and_11_out, nor_1_out);
  nor nor_1 (nor_1_out, in_1[2], in_1[3], in_1[4]);
  and and_13 (and_13_out, or_5_out, or_6_out);
  nor nor_2 (nor_2_out, in_1[5], in_1[6], in_1[7]);
  or or_6 (or_6_out, nor_2_out, and_12_out);
  and and_14 (and_14_out, OPCODE_0, comparator_24_eq);
  Comparator #(.width(11)) comparator_24 (
    .a(11'h2a), .b({in_1[18:16], in_1[31:24]}), .eq(comparator_24_eq));  // open: gt, lt
  Comparator #(.width(6)) comparator_25 (.a(6'b001010), .b(in_1[7:2]), .eq(comparator_25_eq));  // open: gt, lt
  and and_15 (and_15_out, OPCODE_0, comparator_26_eq);
  Comparator #(.width(11)) comparator_26 (
    .a(11'h24), .b({in_1[18:16], in_1[31:24]}), .eq(comparator_26_eq));  // open: gt, lt
  Comparator #(.width(6)) comparator_27 (.a(6'b001100), .b(in_1[7:2]), .eq(comparator_27_eq));  // open: gt, lt
  Comparator #(.width(6)) comparator_28 (.a(6'b100011), .b(in_1[7:2]), .eq(lw));  // open: gt, lt
  Comparator #(.width(16)) comparator_29 (
    .a(16'he000), .b({in_1[7:0], in_1[15:8]}), .eq(comparator_29_eq));  // open: gt, lt
  and and_16 (pop, comparator_29_eq, comparator_30_eq);
  Comparator #(.width(11)) comparator_30 (
    .a({11{1'b0}}), .b({in_1[18:16], in_1[31:24]}), .eq(comparator_30_eq));  // open: gt, lt
  Comparator #(.width(6)) comparator_31 (.a(6'b001000), .b(in_1[7:2]), .gt(comparator_31_gt));  // open: eq, lt
  or or_7 (or_7_out, comparator_32_gt, comparator_32_lt);
  Comparator #(.width(6)) comparator_32 (
    .a(in_1[7:2]), .b(6'b000011), .gt(comparator_32_gt), .lt(comparator_32_lt));  // open: eq
  Comparator #(.width(6)) comparator_33 (.a(in_1[7:2]), .b({6{1'b0}}), .gt(comparator_33_gt));  // open: eq, lt
  Multiplexer #(.width(32), .enable("false")) multiplexer_4 (
    .in0({multiplexer_3_out, in_1[23:16], in_1[31:24]}),
    .in1({{6{1'b0}}, in_1[1:0], in_1[15:8], in_1[23:16], in_1[31:24]}), .out(k), .sel(j));
  or or_8 (Inm, comparator_23_eq, ~and_13_out);  // OR_Gate
  or or_9 (stl, and_14_out, comparator_25_eq);
  or or_10 (\and , and_15_out, comparator_27_eq);
  Comparator #(.width(6)) comparator_34 (.a(6'b000001), .b(in_1[7:2]), .eq(bltz));  // open: gt, lt
  and and_17 (and_17_out, comparator_31_gt, or_7_out, comparator_33_gt);
  Comparator #(.width(11)) comparator_35 (
    .a(11'h2b), .b({in_1[18:16], in_1[31:24]}), .eq(comparator_35_eq));  // open: gt, lt
  Comparator #(.width(11)) comparator_36 (
    .a(11'h25), .b({in_1[18:16], in_1[31:24]}), .eq(comparator_36_eq));  // open: gt, lt
  Comparator #(.width(6)) comparator_37 (.a(6'b101011), .b(in_1[7:2]), .eq(sw));  // open: gt, lt
  or or_11 (jump, and_17_out, comparator_38_eq);
  Comparator #(.width(27)) comparator_38 (
    .a({in_1[7:2], in_1[12:8], in_1[23:16], in_1[31:24]}), .b(27'h8), .eq(comparator_38_eq));  // open: gt, lt
  nor nor_3 (save, beq, bne, blez, bgtz, bltz, j, jr, sw, push, halt, tty, mulu, mul, divu, div, lw);
  or or_12 (ESCRIBIR_EN_RAM, sw, push);
  and and_18 (and_18_out, OPCODE_0, comparator_35_eq);
  or or_13 (stlu, and_18_out, comparator_39_eq);
  Comparator #(.width(6)) comparator_39 (.a(6'b001011), .b(in_1[7:2]), .eq(comparator_39_eq));  // open: gt, lt
  and and_19 (and_19_out, OPCODE_0, comparator_36_eq);
  or or_14 (\or , and_19_out, comparator_40_eq);
  Comparator #(.width(6)) comparator_40 (.a(6'b001101), .b(in_1[7:2]), .eq(comparator_40_eq));  // open: gt, lt
  Comparator #(.width(6)) comparator_41 (.a(6'b111000), .b(in_1[7:2]), .eq(comparator_41_eq));  // open: gt, lt
  and and_20 (push, comparator_41_eq, comparator_42_eq);
  Comparator #(.width(21)) comparator_42 (
    .a(21'h1), .b({in_1[12:8], in_1[23:16], in_1[31:24]}), .eq(comparator_42_eq));  // open: gt, lt
  or or_15 (VARIARA_SP, pop, push);
  Comparator #(.width(6)) comparator_43 (.a(6'b000010), .b(in_1[7:2]), .eq(j));  // open: gt, lt
  Priority_Encoder #(.select(5), .disabled(0)) priority_encoder_1 (
    .in0(1'b1), .in1(add), .in2(sub), .in3(mul), .in4(mulu), .in5(div), .in6(divu), .in7(stl), .in8(stlu),
    .in9(\and ), .in10(\or ), .in11(\nor ), .in12(\xor ), .in13(beq), .in14(bne), .in15(blez), .in16(bgtz),
    .in17(bltz), .in18(j), .in19(jr), .in20(mflo), .in21(mfhi), .in22(lw), .in23(sw), .in24(pop),
    .in25(push), .in26(halt), .in27(tty), .in28(rnd), .in29(kbd), .in30(1'b0), .in31(1'b0), .out(out_4));  // open: gs, en_out, en_in
  and and_21 (and_21_out, OPCODE_0, comparator_44_eq);
  Comparator #(.width(11)) comparator_44 (
    .a(11'h28), .b({in_1[18:16], in_1[31:24]}), .eq(comparator_44_eq));  // open: gt, lt
  Comparator #(.width(6)) comparator_45 (.a(6'b001110), .b(in_1[7:2]), .eq(comparator_45_eq));  // open: gt, lt
  and and_22 (\nor , OPCODE_0, comparator_46_eq);
  Comparator #(.width(11)) comparator_46 (
    .a(11'h27), .b({in_1[18:16], in_1[31:24]}), .eq(comparator_46_eq));  // open: gt, lt
  Comparator #(.width(11)) comparator_47 (
    .a(11'h10), .b({in_1[18:16], in_1[31:24]}), .eq(comparator_47_eq));  // open: gt, lt
  and and_23 (mfhi, comparator_47_eq, comparator_48_eq);
  Comparator #(.width(16)) comparator_48 (
    .a({16{1'b0}}), .b({in_1[7:0], in_1[15:8]}), .eq(comparator_48_eq));  // open: gt, lt
  and and_24 (mflo, comparator_48_eq, comparator_49_eq);
  Comparator #(.width(11)) comparator_49 (
    .a(11'h12), .b({in_1[18:16], in_1[31:24]}), .eq(comparator_49_eq));  // open: gt, lt
  or or_16 (LEER_RAM, lw, pop);
  or or_17 (\xor , and_21_out, comparator_45_eq);
  Comparator #(.width(21)) comparator_50 (
    .a(21'h8), .b({in_1[12:8], in_1[23:16], in_1[31:24]}), .eq(jr));  // open: gt, lt

  assign A = {in_1[1:0], in_1[15:13]};

  // Other names for the same wires on the sheet: Instruction[31:0] = in_1;
  //   J_Value[25:0] = {in_1[1:0], in_1[15:8], in_1[23:16], in_1[31:24]}; RS[4:0] = {in_1[1:0], in_1[15:13]};
  //   Start[15:0] = {in_1[7:0], in_1[15:8]}; Big_part_of_it[20:0] = {in_1[12:8], in_1[23:16], in_1[31:24]};
  //   End[10:0] = {in_1[18:16], in_1[31:24]}; Func_Code[5:0] = in_1[29:24];
  //   IConstant[15:0] = {in_1[23:16], in_1[31:24]}; x[4:0] = {in_1[18:16], in_1[31:30]}; RD[4:0] = in_1[23:19];
  //   RT[4:0] = in_1[12:8]; Op_Code[5:0] = in_1[7:2]

  // Notes on the sheet:
  //   OPERADORES
  //   RANDOM
  //   ADD
  //   MUL
  //   MULU
  //   OPERACIONES ESPECIALES
  //   Halt
  //   BEQ
  //   BNE
  //   SEPARANDO LA ENTRADA
  //   OBTENIENDO DIRECCION
  //   EN LA CUAL SE ESCRIBE
  //   auxiliares
  //   SUB
  //   DIV
  //   DIVU
  //   SET KEY
  //   TTY
  //   BLEZ
  //   BGTZ
  //   CONSTANTE k
  //   LOAD W
  //   POP FROM STACK
  //   INMEDIATE
  //   OPERATION
  //   STL
  //   AND
  //   READ/WRITE
  //   OPERACIONES BRANCH
  //   INSTRUCCION DE SALTO
  //   STORE W
  //   PUSH IN STAK
  //   BLTZ
  //   GUARDA
  //   EN RF
  //   STLU
  //   OR
  //   JUMP
  //   OPERACIONES ARITMETICAS
  //   OPERACIONES
  //   DA LA OPERACION
  //   XOR
  //   NOR
  //   OPERACIONES MOVE
  //   MOVE LO
  //   MOVE HI
  //   REG
  //   JUMP
  //   JUMP
endmodule

module READER (
  input  [31:0] in_1,
  input  [31:0] in_2,
  input  [31:0] in_3,
  input  [31:0] ALU,
  input  [4:0] in_5,
  input  in_6,
  input  in_7,
  input  [31:0] in_8,
  input  in_9,
  input  [4:0] in_10,
  input  DEBE_GUARDARSE,
  output [31:0] out_12,
  output [31:0] out_13,
  output [4:0] out_14,
  output out_15
);

  wire d_ff_1_q, lw, or_1_out, or_2_out, pop;
  wire [2:2] comparator_1_eq;
  wire [4:0] register_1_q;
  wire [31:0] adder_1_out, adder_2_out, multiplexer_2_out, multiplexer_3_out;

  Comparator #(.width(5)) comparator_1 (.a(out_14), .b({5{1'b1}}), .eq(comparator_1_eq[2]));  // open: gt, lt
  Multiplexer #(.width(32), .enable("false")) multiplexer_1 (
    .in0(ALU), .in1(multiplexer_2_out), .out(out_12), .sel(in_6));
  Adder #(.width(32)) adder_1 (
    .a({in_8[7:0], in_8[15:8], in_8[23:16], in_8[31:24]}), .b({{29{1'b0}}, comparator_1_eq[2], 2'b00}),
    .out(adder_1_out));  // open: cin, cout
  Multiplexer #(.width(32), .enable("false")) multiplexer_2 (
    .in0({in_8[7:0], in_8[15:8], in_8[23:16], in_8[31:24]}), .in1(adder_1_out), .out(multiplexer_2_out),
    .sel(d_ff_1_q));
  D_Flip_Flop #(.trigger("falling")) d_ff_1 (.Q(d_ff_1_q), .preset(pop), .reset(lw));  // open: clk, D, Qn, en
  Adder #(.width(32)) adder_2 (.a(in_1), .b(in_3), .out(adder_2_out));  // open: cin, cout
  or or_1 (or_1_out, lw, pop);
  Multiplexer #(.width(32), .enable("false")) multiplexer_3 (
    .in0(adder_2_out), .in1(in_2), .out(multiplexer_3_out), .sel(pop));
  or or_2 (or_2_out, pop, lw);
  Multiplexer #(.width(5), .enable("false")) multiplexer_4 (.in0(in_10), .in1(register_1_q), .out(out_14), .sel(in_6));
  Register #(.width(5), .trigger("falling")) register_1 (
    .D(in_10), .en(or_1_out), .Q(register_1_q), .clk(in_7), .clr(in_9));
  Register #(.width(32), .trigger("falling")) register_2 (
    .D(multiplexer_3_out), .en(or_2_out), .Q(out_13), .clk(in_7), .clr(in_9));
  Comparator #(.width(5)) comparator_2 (.a(5'b10110), .b(in_5), .eq(lw));  // open: gt, lt
  Comparator #(.width(5)) comparator_3 (.a(5'b11000), .b(in_5), .eq(pop));  // open: gt, lt
  or or_3 (out_15, DEBE_GUARDARSE, in_6);

  // Other names for the same wires on the sheet: A[31:0] = in_1; B[31:0] = in_2; CLK = in_7; k[31:0] = in_3;
  //   r31[4:0] = out_14; Read = in_6; RST = in_9

  // Notes on the sheet:
  //   RAM
  //   VALOR A GUARDAR
  //   READER
  //   DONDE LEE
  //   DIRECCION A GUARDAR
  //   ES OP DE LECTURA
endmodule

module Register_File (
  input  [4:0] INPUTS,
  input  [4:0] in_2,
  input  in_3,
  input  [31:0] in_4,
  input  in_5,
  input  [4:0] in_6,
  input  in_7,
  input  in_8,
  output [31:0] A,
  output [31:0] B
);

  wire and_1_out, and_2_out, and_3_out, and_4_out, and_5_out, and_6_out, and_9_out, and_10_out, and_11_out,
       and_12_out, and_13_out, and_14_out, and_15_out, and_16_out, and_17_out, and_18_out, and_19_out,
       and_20_out, and_21_out, and_22_out, and_23_out, and_24_out, and_25_out, and_26_out, and_27_out,
       and_28_out, and_29_out, and_30_out, and_31_out, and_32_out, and_33_out, comparator_1_eq,
       comparator_2_eq, comparator_3_eq, comparator_4_eq, comparator_5_eq, comparator_6_eq, comparator_7_eq,
       comparator_8_eq, comparator_9_eq, comparator_10_eq, comparator_11_eq, comparator_12_eq,
       comparator_13_eq, comparator_14_eq, comparator_15_eq, comparator_16_eq, comparator_17_eq,
       comparator_18_eq, comparator_19_eq, comparator_20_eq, comparator_21_eq, comparator_22_eq,
       comparator_23_eq, comparator_24_eq, comparator_25_eq, comparator_26_eq, comparator_27_eq,
       comparator_28_eq, comparator_29_eq, comparator_30_eq, comparator_31_eq, RW;
  wire [0:0] and_7_out;
  wire [31:0] _0, _1, _2, _3, _4, _5, _6, _7, _8, _9, _10, _11, _12, _13, _14, _15, _16, _17, _18, _19, _20,
       _21, _22, _23, _24, _25, _26, _27, _28, _29, _30, _31, adder_1_out, multiplexer_1_out,
       multiplexer_2_out, register_7_q, subtractor_1_out;

  Multiplexer #(.width(32), .enable("false")) multiplexer_1 (
    .in0(32'hfffffffc), .in1(32'h4), .out(multiplexer_1_out), .sel(in_7));
  Comparator #(.width(5)) comparator_1 (.a(in_6), .b(5'b00001), .eq(comparator_1_eq));  // open: gt, lt
  and and_1 (and_1_out, comparator_1_eq, RW);
  and and_2 (and_2_out, comparator_2_eq, RW);
  Comparator #(.width(5)) comparator_2 (.a(in_6), .b(5'b00110), .eq(comparator_2_eq));  // open: gt, lt
  and and_3 (and_3_out, comparator_3_eq, RW);
  Comparator #(.width(5)) comparator_3 (.a(in_6), .b(5'b01011), .eq(comparator_3_eq));  // open: gt, lt
  Comparator #(.width(5)) comparator_4 (.a(in_6), .b(5'b10000), .eq(comparator_4_eq));  // open: gt, lt
  and and_4 (and_4_out, comparator_4_eq, RW);
  and and_5 (and_5_out, comparator_5_eq, RW);
  Comparator #(.width(5)) comparator_5 (.a(in_6), .b(5'b10101), .eq(comparator_5_eq));  // open: gt, lt
  Comparator #(.width(5)) comparator_6 (.a(in_6), .b(5'b11010), .eq(comparator_6_eq));  // open: gt, lt
  and and_6 (and_6_out, comparator_6_eq, RW);
  Adder #(.width(32)) adder_1 (.a(register_7_q), .b(multiplexer_1_out), .out(adder_1_out));  // open: cin, cout
  Register #(.width(32), .trigger("falling")) register_1 (.D(in_4), .en(and_1_out), .Q(_1), .clk(in_5), .clr(in_3));
  Register #(.width(32), .trigger("falling")) register_2 (.D(in_4), .en(and_2_out), .Q(_6), .clk(in_5), .clr(in_3));
  Register #(.width(32), .trigger("falling")) register_3 (.D(in_4), .en(and_3_out), .Q(_11), .clk(in_5), .clr(in_3));
  Register #(.width(32), .trigger("falling")) register_4 (.D(in_4), .en(and_4_out), .Q(_16), .clk(in_5), .clr(in_3));
  Register #(.width(32), .trigger("falling")) register_5 (.D(in_4), .en(and_5_out), .Q(_21), .clk(in_5), .clr(in_3));
  Register #(.width(32), .trigger("falling")) register_6 (.D(in_4), .en(and_6_out), .Q(_26), .clk(in_5), .clr(in_3));
  Comparator #(.width(5)) comparator_7 (.a(in_6), .b({5{1'b1}}), .eq(comparator_7_eq));  // open: gt, lt
  and and_7 (and_7_out[0], comparator_7_eq, in_7);
  Comparator #(.width(5)) comparator_8 (.a(in_6), .b(5'b00010), .eq(comparator_8_eq));  // open: gt, lt
  Comparator #(.width(5)) comparator_9 (.a(in_6), .b(5'b00111), .eq(comparator_9_eq));  // open: gt, lt
  Comparator #(.width(5)) comparator_10 (.a(in_6), .b(5'b01100), .eq(comparator_10_eq));  // open: gt, lt
  Comparator #(.width(5)) comparator_11 (.a(in_6), .b(5'b10001), .eq(comparator_11_eq));  // open: gt, lt
  Comparator #(.width(5)) comparator_12 (.a(in_6), .b(5'b10110), .eq(comparator_12_eq));  // open: gt, lt
  Comparator #(.width(5)) comparator_13 (.a(in_6), .b(5'b11011), .eq(comparator_13_eq));  // open: gt, lt
  and and_8 (RW, in_7, ~in_8);  // AND_Gate
  Register #(.width(32), .trigger("falling")) register_7 (
    .D(multiplexer_2_out), .en(1'b1), .Q(register_7_q), .clk(in_5), .clr(in_3));
  Multiplexer #(.select(2), .width(32), .enable("false")) multiplexer_2 (
    .in0(register_7_q), .in1(in_4), .in2(adder_1_out), .in3(adder_1_out), .out(multiplexer_2_out),
    .sel({in_8, and_7_out[0]}));
  and and_9 (and_9_out, comparator_8_eq, RW);
  and and_10 (and_10_out, comparator_9_eq, RW);
  and and_11 (and_11_out, comparator_10_eq, RW);
  and and_12 (and_12_out, comparator_11_eq, RW);
  and and_13 (and_13_out, comparator_12_eq, RW);
  and and_14 (and_14_out, comparator_13_eq, RW);
  Register #(.width(32), .trigger("falling")) register_8 (.Q(_0), .clk(in_5), .clr(in_3));  // open: D, en
  Subtractor #(.width(32)) subtractor_1 (.a(register_7_q), .b(32'h4), .out(subtractor_1_out));  // open: bin, bout
  Register #(.width(32), .trigger("falling")) register_9 (.D(in_4), .en(and_9_out), .Q(_2), .clk(in_5), .clr(in_3));
  Register #(.width(32), .trigger("falling")) register_10 (.D(in_4), .en(and_10_out), .Q(_7), .clk(in_5), .clr(in_3));
  Register #(.width(32), .trigger("falling")) register_11 (.D(in_4), .en(and_11_out), .Q(_12), .clk(in_5), .clr(in_3));
  Register #(.width(32), .trigger("falling")) register_12 (.D(in_4), .en(and_12_out), .Q(_17), .clk(in_5), .clr(in_3));
  Register #(.width(32), .trigger("falling")) register_13 (.D(in_4), .en(and_13_out), .Q(_22), .clk(in_5), .clr(in_3));
  Register #(.width(32), .trigger("falling")) register_14 (.D(in_4), .en(and_14_out), .Q(_27), .clk(in_5), .clr(in_3));
  Multiplexer #(.width(32), .enable("false")) multiplexer_3 (
    .in0(register_7_q), .in1(subtractor_1_out), .out(_31), .sel(and_15_out));
  and and_15 (and_15_out, ~in_7, in_8);  // AND_Gate
  Comparator #(.width(5)) comparator_14 (.a(in_6), .b(5'b00011), .eq(comparator_14_eq));  // open: gt, lt
  Comparator #(.width(5)) comparator_15 (.a(in_6), .b(5'b01000), .eq(comparator_15_eq));  // open: gt, lt
  Comparator #(.width(5)) comparator_16 (.a(in_6), .b(5'b01101), .eq(comparator_16_eq));  // open: gt, lt
  Comparator #(.width(5)) comparator_17 (.a(in_6), .b(5'b10010), .eq(comparator_17_eq));  // open: gt, lt
  Comparator #(.width(5)) comparator_18 (.a(in_6), .b(5'b10111), .eq(comparator_18_eq));  // open: gt, lt
  Comparator #(.width(5)) comparator_19 (.a(in_6), .b(5'b11100), .eq(comparator_19_eq));  // open: gt, lt
  Register #(.width(32), .trigger("falling")) register_15 (.D(in_4), .en(and_16_out), .Q(_3), .clk(in_5), .clr(in_3));
  and and_16 (and_16_out, comparator_14_eq, RW);
  Register #(.width(32), .trigger("falling")) register_16 (.D(in_4), .en(and_17_out), .Q(_8), .clk(in_5), .clr(in_3));
  and and_17 (and_17_out, comparator_15_eq, RW);
  Register #(.width(32), .trigger("falling")) register_17 (.D(in_4), .en(and_18_out), .Q(_13), .clk(in_5), .clr(in_3));
  and and_18 (and_18_out, comparator_16_eq, RW);
  Register #(.width(32), .trigger("falling")) register_18 (.D(in_4), .en(and_19_out), .Q(_18), .clk(in_5), .clr(in_3));
  and and_19 (and_19_out, comparator_17_eq, RW);
  Register #(.width(32), .trigger("falling")) register_19 (.D(in_4), .en(and_20_out), .Q(_23), .clk(in_5), .clr(in_3));
  and and_20 (and_20_out, comparator_18_eq, RW);
  Register #(.width(32), .trigger("falling")) register_20 (.D(in_4), .en(and_21_out), .Q(_28), .clk(in_5), .clr(in_3));
  and and_21 (and_21_out, comparator_19_eq, RW);
  Multiplexer #(.select(5), .width(32), .enable("false")) multiplexer_4 (
    .in0(_0), .in1(_1), .in2(_2), .in3(_3), .in4(_4), .in5(_5), .in6(_6), .in7(_7), .in8(_8), .in9(_9),
    .in10(_10), .in11(_11), .in12(_12), .in13(_13), .in14(_14), .in15(_15), .in16(_16), .in17(_17),
    .in18(_18), .in19(_19), .in20(_20), .in21(_21), .in22(_22), .in23(_23), .in24(_24), .in25(_25),
    .in26(_26), .in27(_27), .in28(_28), .in29(_29), .in30(_30), .in31(_31), .out(A), .sel(INPUTS));
  Comparator #(.width(5)) comparator_20 (.a(in_6), .b(5'b00100), .eq(comparator_20_eq));  // open: gt, lt
  and and_22 (and_22_out, comparator_20_eq, RW);
  Comparator #(.width(5)) comparator_21 (.a(in_6), .b(5'b01001), .eq(comparator_21_eq));  // open: gt, lt
  and and_23 (and_23_out, comparator_21_eq, RW);
  Comparator #(.width(5)) comparator_22 (.a(in_6), .b(5'b01110), .eq(comparator_22_eq));  // open: gt, lt
  and and_24 (and_24_out, comparator_22_eq, RW);
  and and_25 (and_25_out, comparator_23_eq, RW);
  Comparator #(.width(5)) comparator_23 (.a(in_6), .b(5'b10011), .eq(comparator_23_eq));  // open: gt, lt
  and and_26 (and_26_out, comparator_24_eq, RW);
  Comparator #(.width(5)) comparator_24 (.a(in_6), .b(5'b11000), .eq(comparator_24_eq));  // open: gt, lt
  and and_27 (and_27_out, comparator_25_eq, RW);
  Comparator #(.width(5)) comparator_25 (.a(in_6), .b(5'b11101), .eq(comparator_25_eq));  // open: gt, lt
  Register #(.width(32), .trigger("falling")) register_21 (.D(in_4), .en(and_22_out), .Q(_4), .clk(in_5), .clr(in_3));
  Register #(.width(32), .trigger("falling")) register_22 (.D(in_4), .en(and_23_out), .Q(_9), .clk(in_5), .clr(in_3));
  Register #(.width(32), .trigger("falling")) register_23 (.D(in_4), .en(and_24_out), .Q(_14), .clk(in_5), .clr(in_3));
  Register #(.width(32), .trigger("falling")) register_24 (.D(in_4), .en(and_25_out), .Q(_19), .clk(in_5), .clr(in_3));
  Register #(.width(32), .trigger("falling")) register_25 (.D(in_4), .en(and_26_out), .Q(_24), .clk(in_5), .clr(in_3));
  Register #(.width(32), .trigger("falling")) register_26 (.D(in_4), .en(and_27_out), .Q(_29), .clk(in_5), .clr(in_3));
  Multiplexer #(.select(5), .width(32), .enable("false")) multiplexer_5 (
    .in0(_0), .in1(_1), .in2(_2), .in3(_3), .in4(_4), .in5(_5), .in6(_6), .in7(_7), .in8(_8), .in9(_9),
    .in10(_10), .in11(_11), .in12(_12), .in13(_13), .in14(_14), .in15(_15), .in16(_16), .in17(_17),
    .in18(_18), .in19(_19), .in20(_20), .in21(_21), .in22(_22), .in23(_23), .in24(_24), .in25(_25),
    .in26(_26), .in27(_27), .in28(_28), .in29(_29), .in30(_30), .in31(_31), .out(B), .sel(in_2));
  Comparator #(.width(5)) comparator_26 (.a(in_6), .b(5'b00101), .eq(comparator_26_eq));  // open: gt, lt
  Comparator #(.width(5)) comparator_27 (.a(in_6), .b(5'b01010), .eq(comparator_27_eq));  // open: gt, lt
  Comparator #(.width(5)) comparator_28 (.a(in_6), .b(5'b01111), .eq(comparator_28_eq));  // open: gt, lt
  Comparator #(.width(5)) comparator_29 (.a(in_6), .b(5'b10100), .eq(comparator_29_eq));  // open: gt, lt
  Comparator #(.width(5)) comparator_30 (.a(in_6), .b(5'b11001), .eq(comparator_30_eq));  // open: gt, lt
  Comparator #(.width(5)) comparator_31 (.a(in_6), .b(5'b11110), .eq(comparator_31_eq));  // open: gt, lt
  Register #(.width(32), .trigger("falling")) register_27 (.D(in_4), .en(and_28_out), .Q(_5), .clk(in_5), .clr(in_3));
  and and_28 (and_28_out, comparator_26_eq, RW);
  Register #(.width(32), .trigger("falling")) register_28 (.D(in_4), .en(and_29_out), .Q(_10), .clk(in_5), .clr(in_3));
  and and_29 (and_29_out, comparator_27_eq, RW);
  Register #(.width(32), .trigger("falling")) register_29 (.D(in_4), .en(and_30_out), .Q(_15), .clk(in_5), .clr(in_3));
  and and_30 (and_30_out, comparator_28_eq, RW);
  Register #(.width(32), .trigger("falling")) register_30 (.D(in_4), .en(and_31_out), .Q(_20), .clk(in_5), .clr(in_3));
  and and_31 (and_31_out, comparator_29_eq, RW);
  Register #(.width(32), .trigger("falling")) register_31 (.D(in_4), .en(and_32_out), .Q(_25), .clk(in_5), .clr(in_3));
  and and_32 (and_32_out, comparator_30_eq, RW);
  Register #(.width(32), .trigger("falling")) register_32 (.D(in_4), .en(and_33_out), .Q(_30), .clk(in_5), .clr(in_3));
  and and_33 (and_33_out, comparator_31_eq, RW);

  // Other names for the same wires on the sheet: pp = in_8; AD[4:0] = in_6; CLK = in_5; Input_value[31:0] = in_4;
  //   RST = in_3; RWI = in_7; SA[4:0] = INPUTS; SB[4:0] = in_2

  // Notes on the sheet:
  //   REG:1
  //   REG:6
  //   REG:11
  //   REG:16
  //   REG:21
  //   REG:26
  //   REGISTER FILE
  //   REG:2
  //   REG:7
  //   REG:12
  //   REG:17
  //   REG:22
  //   REG:27
  //   REG:0
  //   REG:31(SP)
  //   REG:3
  //   REG:8
  //   REG:13
  //   REG:18
  //   REG:23
  //   REG:28
  //   Outputs
  //   REG:4
  //   REG:9
  //   REG:14
  //   REG:19
  //   REG:24
  //   REG:29
  //   REG:5
  //   REG:10
  //   REG:15
  //   REG:20
  //   REG:25
  //   REG:30
endmodule

module ALU (
  input  [31:0] in_1,
  input  [31:0] in_2,
  input  [31:0] in_3,
  input  in_4,
  input  in_5,
  input  [6:0] in_6,
  input  in_7,
  input  [4:0] in_8,
  input  in_9,
  output Cond,
  output [31:0] Result,
  output [31:0] Jump_size,
  output Stop,
  output [6:0] TTY,
  output Enable
);

  wire beq, bgtz, blez, bltz, bne, comparator_3_eq, comparator_6_gt, comparator_7_gt, comparator_9_eq, MOD,
       xor_2_out, xor_3_out, xor_4_out;
  wire [0:0] stlResult, stluResult;
  wire [6:0] kbd, KBD_DD;
  wire [31:0] addResult, andResult, Au, B, Bu, divider_1_out, divider_1_rem, HId, HIdu, HIm, HImu, LOd, LOdu,
       LOm, LOmu, mfhiResult, mfloResult, multiplexer_7_out, multiplexer_10_out, multiplier_1_cout,
       multiplier_1_out, negador_1_output, negador_2_output, negator_1_out, negator_2_out, negator_3_out,
       negator_4_out, norResult, orResult, rndResult, subResult, xorResult;

  Comparator #(.width(32)) comparator_1 (.a(in_1), .b(in_2), .eq(beq));  // open: gt, lt
  not not_1 (bne, beq);
  not not_2 (blez, bgtz);
  Comparator #(.width(32)) comparator_2 (.a(in_1), .b({32{1'b0}}), .gt(bgtz), .lt(bltz));  // open: eq
  Multiplexer #(.width(32), .enable("false")) multiplexer_1 (
    .in0(B), .in1(in_1), .out(Jump_size), .sel(comparator_3_eq));
  Comparator #(.width(5)) comparator_3 (.a(5'b10011), .b(in_8), .eq(comparator_3_eq));  // open: gt, lt
  assign andResult = in_1 & B;  // AND_Gate and_1, 32 bits wide
  assign orResult = in_1 | B;  // OR_Gate or_1, 32 bits wide
  Multiplexer #(.select(5), .enable("false")) multiplexer_2 (
    .in0(1'b0), .in1(1'b0), .in2(1'b0), .in3(1'b0), .in4(1'b0), .in5(1'b0), .in6(1'b0), .in7(1'b0),
    .in8(1'b0), .in9(1'b0), .in10(1'b0), .in11(1'b0), .in12(1'b0), .in13(beq), .in14(bne), .in15(blez),
    .in16(bgtz), .in17(bltz), .in18(1'b0), .in19(1'b1), .in20(1'b0), .in21(1'b0), .in22(1'b0), .in23(1'b0),
    .in24(1'b0), .in25(1'b0), .in26(1'b0), .in27(1'b0), .in28(1'b0), .in29(1'b0), .in30(1'b0), .in31(1'b0),
    .out(Cond), .sel(in_8));
  assign norResult = ~(in_1 | B);  // NOR_Gate nor_1, 32 bits wide
  assign xorResult = in_1 ^ B;  // XOR_Gate xor_1, 32 bits wide
  Adder #(.width(32)) adder_1 (.a(in_1), .b(B), .out(addResult));  // open: cin, cout
  Comparator #(.width(32)) comparator_4 (.a(in_1), .b(B), .lt(stlResult[0]));  // open: gt, eq
  Multiplexer #(.select(5), .width(32), .enable("false")) multiplexer_3 (
    .in0({32{1'b0}}), .in1(addResult), .in2(subResult), .in3({32{1'b0}}), .in4({32{1'b0}}), .in5({32{1'b0}}),
    .in6({32{1'b0}}), .in7({{31{1'b0}}, stlResult[0]}), .in8({{31{1'b0}}, stluResult[0]}), .in9(andResult),
    .in10(orResult), .in11(norResult), .in12(xorResult), .in13({32{1'b0}}), .in14({32{1'b0}}),
    .in15({32{1'b0}}), .in16({32{1'b0}}), .in17({32{1'b0}}), .in18({32{1'b0}}), .in19({32{1'b0}}),
    .in20(mfloResult), .in21(mfhiResult), .in22({32{1'b0}}), .in23({32{1'b0}}), .in24({32{1'b0}}),
    .in25({32{1'b0}}), .in26({32{1'b0}}), .in27({32{1'b0}}), .in28(rndResult), .in29({{25{1'b0}}, kbd}),
    .in30({32{1'b0}}), .in31({32{1'b0}}), .out(Result), .sel(in_8));
  Multiplexer #(.width(32), .enable("false")) multiplexer_4 (.in0(in_2), .in1(in_3), .out(B), .sel(in_4));
  Subtractor #(.width(32)) subtractor_1 (.a(in_1), .b(B), .out(subResult));  // open: bin, bout
  Comparator #(.width(32), .mode("unsigned")) comparator_5 (.a(in_1), .b(B), .lt(stluResult[0]));  // open: gt, eq
  Multiplexer #(.width(32), .enable("false")) multiplexer_5 (
    .in0(multiplier_1_cout), .in1(negador_1_output), .out(HIm), .sel(xor_2_out));
  xor xor_2 (xor_2_out, in_1[31], B[31]);
  negador negador_1 (.in_1(multiplier_1_cout), .Output(negador_1_output));
  Multiplexer #(.width(32), .enable("false")) multiplexer_6 (
    .in0(divider_1_rem), .in1(negador_2_output), .out(HId), .sel(in_1[31]));
  negador negador_2 (.in_1(divider_1_rem), .Output(negador_2_output));
  Register #(.width(32)) register_1 (.D(multiplexer_7_out), .en(MOD), .Q(mfhiResult), .clk(in_5), .clr(in_9));
  Multiplexer #(.select(3), .width(32), .enable("false")) multiplexer_7 (
    .in3(HIm), .in4(HImu), .in5(HId), .in6(HIdu), .out(multiplexer_7_out), .sel(in_8[2:0]));  // open: in0, in1, in2, in7
  Comparator #(.width(5)) comparator_6 (.a(5'b00111), .b(in_8), .gt(comparator_6_gt));  // open: eq, lt
  and and_2 (MOD, comparator_6_gt, comparator_7_gt);
  Comparator #(.width(5)) comparator_7 (.a(in_8), .b(5'b00010), .gt(comparator_7_gt));  // open: eq, lt
  Multiplier #(.width(32)) multiplier_1 (
    .a(Au), .b(Bu), .out(multiplier_1_out), .cout(multiplier_1_cout));  // open: cin
  Divider #(.width(32)) divider_1 (.a(Au), .b(Bu), .out(divider_1_out), .rem(divider_1_rem));  // open: upper
  Negator #(.width(32)) negator_1 (.in(divider_1_out), .out(negator_1_out));
  Comparator #(.width(5)) comparator_8 (.a(5'b11011), .b(in_8), .eq(Enable));  // open: gt, lt
  Multiplexer #(.width(32), .enable("false")) multiplexer_8 (
    .in0(multiplier_1_out), .in1(negator_2_out), .out(LOm), .sel(xor_3_out));
  Negator #(.width(32)) negator_2 (.in(multiplier_1_out), .out(negator_2_out));
  xor xor_3 (xor_3_out, in_1[31], B[31]);
  Multiplexer #(.width(32), .enable("false")) multiplexer_9 (
    .in0(divider_1_out), .in1(negator_1_out), .out(LOd), .sel(xor_4_out));
  xor xor_4 (xor_4_out, in_1[31], B[31]);
  Random #(.width(32)) random_1 (.clk(in_5), .next(1'b1), .out(rndResult));  // open: clr
  Register #(.width(32)) register_2 (.D(multiplexer_10_out), .en(MOD), .Q(mfloResult), .clk(in_5), .clr(in_9));
  Multiplexer #(.select(3), .width(32), .enable("false")) multiplexer_10 (
    .in3(LOm), .in4(LOmu), .in5(LOd), .in6(LOdu), .out(multiplexer_10_out), .sel(in_8[2:0]));  // open: in0, in1, in2, in7
  Multiplexer #(.width(32), .enable("false")) multiplexer_11 (.in0(B), .in1(negator_3_out), .out(Bu), .sel(B[31]));
  Negator #(.width(32)) negator_3 (.in(B), .out(negator_3_out));
  Multiplexer #(.width(32), .enable("false")) multiplexer_12 (
    .in0(in_1), .in1(negator_4_out), .out(Au), .sel(in_1[31]));
  Negator #(.width(32)) negator_4 (.in(in_1), .out(negator_4_out));
  Multiplier #(.width(32)) multiplier_2 (.a(in_1), .b(B), .out(LOmu), .cout(HImu));  // open: cin
  Divider #(.width(32)) divider_2 (.a(in_1), .b(B), .out(LOdu), .rem(HIdu));  // open: upper
  D_Flip_Flop #(.trigger("falling")) d_ff_1 (
    .clk(in_5), .D(comparator_9_eq), .Q(Stop), .en(comparator_9_eq), .reset(in_9));  // open: Qn, preset
  Comparator #(.width(5)) comparator_9 (.a(5'b11010), .b(in_8), .eq(comparator_9_eq));  // open: gt, lt
  Multiplexer #(.width(7), .enable("false")) multiplexer_13 (.in0({7{1'b1}}), .in1(KBD_DD), .out(kbd), .sel(in_7));

  assign TTY = in_1[6:0];

  // Other names for the same wires on the sheet: A[31:0] = in_1; As = in_1[31]; Bs = B[31]; CLK = in_5;
  //   k[31:0] = in_3; KBD_AVAILABLE = in_7; KBDD[6:0] = in_6; nB[31:0] = in_2; op[4:0] = in_8; RST = in_9

  // Notes on the sheet:
  //   ALU
  //   Salida para Branch control
  //   Entrada
  //   SUMA
  //   SET LESS THAN
  //   Salida para Register File
  //   OPERACIONES ARITMETICAS Y LOGICAS
  //   RESTA
  //   SET LESS THAN(U)
  //   CARGAR/GUARDAR HI
  //   MULTIPLICACION O DIVISION
  //   MULTIPLICACION
  //   DIVISION
  //   REGISTROS AUXILIARES
  //   OPERACIONES ESPECIALES
  //   RND
  //   TTY
  //   STOP
  //   CARGAR/GUARDAR LO
  //   MULTIPLICACION(U)
  //   DIVISION(U)
  //   KBD
endmodule

module WRITER (
  input  [31:0] in_1,
  input  [31:0] in_2,
  input  in_3,
  input  in_4,
  input  [31:0] in_5,
  input  [4:0] in_6,
  output [31:0] out_7,
  output [31:0] out_8,
  output [31:0] SALIDA,
  output [31:0] out_10,
  output [31:0] out_11
);

  wire or_1_out, or_2_out, push, sw;
  wire [31:0] adder_1_out, multiplexer_1_out, multiplexer_2_out;

  Multiplexer #(.width(32), .enable("false")) multiplexer_1 (.in0(in_1), .in1(in_5), .out(multiplexer_1_out), .sel(sw));
  or or_1 (or_1_out, sw, push);
  Comparator #(.width(5)) comparator_1 (.a(5'b10111), .b(in_6), .eq(sw));  // open: gt, lt
  Comparator #(.width(5)) comparator_2 (.a(5'b11001), .b(in_6), .eq(push));  // open: gt, lt
  Register #(.width(32), .trigger("falling")) register_1 (
    .D(multiplexer_1_out), .en(or_1_out), .Q({out_8[7:0], out_8[15:8], out_8[23:16], out_8[31:24]}),
    .clk(in_3), .clr(in_4));
  Multiplexer #(.width(32), .enable("false")) multiplexer_2 (
    .in0(adder_1_out), .in1(in_5), .out(multiplexer_2_out), .sel(push));
  Adder #(.width(32)) adder_1 (.a(in_1), .b(in_2), .out(adder_1_out));  // open: cin, cout
  Register #(.width(32), .trigger("falling")) register_2 (
    .D(multiplexer_2_out), .en(or_2_out), .Q(out_7), .clk(in_3), .clr(in_4));
  or or_2 (or_2_out, push, sw);

  assign out_10 = out_8;
  assign out_11 = out_8;
  assign SALIDA = out_8;

  // Other names for the same wires on the sheet: A[31:0] = in_1; B[31:0] = in_5; CLK = in_3; k[31:0] = in_2;
  //   RST = in_4

  // Notes on the sheet:
  //   ENTRADA
  //   WRITER
  //   DONDE ESCRIBE
endmodule

module negador (
  input  [31:0] in_1,
  output [31:0] Output
);

  wire [31:0] not_1_out;

  assign not_1_out = ~in_1;  // NOT_Gate not_1, 32 bits wide
  Adder #(.width(32)) adder_1 (.a(not_1_out), .b(32'h1), .out(Output));  // open: cin, cout
endmodule
